// Logisim project part1.circ as structural Verilog: 1 circuit, main circuit main
module main (
);

  wire adder_1_cout, and_1_out, CLK1, CLK2, clock_1_out, comparator_1_lt, counter_1_carry, counter_3_q, HLT,
       INIT, INITCLK, not_1_out, PH1, PH2;
  wire [15:0] adder_1_out, adder_2_out, adder_3_out, adder_4_out, multiplexer_1_out, ram_1_data,
       register_1_q, register_2_q, register_3_q, rom_1_data;
  wire [31:0] counter_2_q;

  Counter #(.width(2), .max('h2), .ongoal("stay")) counter_1 (
    .carry(counter_1_carry), .clk(clock_1_out));  // open: load, D, count, Q, clr
  Clock clock_1 (.out(clock_1_out));
  and and_1 (and_1_out, clock_1_out, ~HLT, counter_1_carry);  // AND_Gate
  not not_1 (not_1_out, and_1_out);
  not not_2 (INIT, counter_1_carry);
  and and_2 (INITCLK, clock_1_out, INIT);
  Counter #(.width(32), .max('hffffffff)) counter_2 (.Q(counter_2_q), .clk(CLK2));  // open: load, D, count, carry, clr
  // Probe on counter_2_q
  Decoder #(.enable("false")) decoder_1 (.out0(PH1), .out1(PH2), .sel(counter_3_q));
  Demultiplexer #(.enable("false")) demultiplexer_1 (.out0(CLK1), .out1(CLK2), .in(and_1_out), .sel(counter_3_q));
  Counter #(.width(1), .max('h1)) counter_3 (.Q(counter_3_q), .clk(not_1_out));  // open: load, D, count, carry, clr
  Adder #(.width(16)) adder_1 (.a(16'h1), .b(register_1_q), .out(adder_1_out), .cout(adder_1_cout));  // open: cin
  // Probe on register_2_q
  Multiplexer #(.width(16), .enable("false")) multiplexer_1 (
    .in0(adder_1_out), .in1({16{1'b0}}), .out(multiplexer_1_out), .sel(INIT));
  // Probe on register_1_q
  Register #(.width(16)) register_1 (.D(adder_3_out), .Q(register_1_q), .clk(CLK2));  // open: en, clr
  Register #(.width(16)) register_2 (.D(rom_1_data), .Q(register_2_q), .clk(INITCLK));  // open: en, clr
  Comparator #(.width(16), .mode("unsigned")) comparator_1 (
    .a(register_1_q), .b(register_2_q), .lt(comparator_1_lt));  // open: gt, eq
  RAM #(.addrWidth(16), .dataWidth(16)) ram_1 (
    .addr(multiplexer_1_out), .data(ram_1_data), .clk(CLK2), .ld(PH1));  // open: sel, clr
  ROM #(.addrWidth(16), .dataWidth(16)) rom_1 (.addr(multiplexer_1_out), .data(rom_1_data));  // open: sel
  // Probe on rom_1_data
  not not_3 (HLT, comparator_1_lt);
  assign ram_1_data = PH2 ? adder_4_out : 16'bz;  // Controlled_Buffer controlled_buffer_1
  Register #(.width(16)) register_3 (.D(ram_1_data), .Q(register_3_q), .clk(CLK1));  // open: en, clr
  Adder #(.width(16)) adder_2 (.a(register_3_q), .b(rom_1_data), .out(adder_2_out));  // open: cin, cout
  // Probe on adder_2_out
  Adder #(.width(16)) adder_3 (.a(adder_2_out), .b(register_1_q), .out(adder_3_out));  // open: cin, cout
  Adder #(.width(16)) adder_4 (.a(16'h1), .b(register_3_q), .out(adder_4_out));  // open: cin, cout

  // Notes on the sheet:
  //   contents of rom_1 (hex, n*v repeats v):
  //   5 0 3 0 1 fffd
endmodule
