// Logisim project part2.circ as structural Verilog: 1 circuit, main circuit main
module main (
);

  wire and_1_out, clock_1_out, comparator_1_lt, comparator_2_lt, not_1_out;
  wire [15:0] adder_1_out, adder_2_out, multiplexer_1_out, ram_1_data, register_1_q;
  wire [31:0] counter_1_q;

  Clock clock_1 (.out(clock_1_out));
  and and_1 (and_1_out, clock_1_out, comparator_2_lt);
  RAM #(.addrWidth(16), .dataWidth(16), .bus("separate")) ram_1 (
    .addr(register_1_q), .din(adder_2_out), .data(ram_1_data), .clk(and_1_out));  // open: str, sel, ld, clr
  Register #(.width(16)) register_1 (.D(adder_1_out), .Q(register_1_q), .clk(and_1_out));  // open: en, clr
  Comparator #(.width(16)) comparator_1 (.a(ram_1_data), .b(16'h3), .lt(comparator_1_lt));  // open: gt, eq
  Adder #(.width(16)) adder_1 (.a(ram_1_data), .b(register_1_q), .out(adder_1_out));  // open: cin, cout
  Comparator #(.width(16), .mode("unsigned")) comparator_2 (
    .a(register_1_q), .b(16'h42e), .lt(comparator_2_lt));  // open: gt, eq
  Adder #(.width(16)) adder_2 (.a(ram_1_data), .b(multiplexer_1_out), .out(adder_2_out));  // open: cin, cout
  Multiplexer #(.width(16), .disabled(0), .enable("false")) multiplexer_1 (
    .in0(16'h1), .in1({16{1'b1}}), .out(multiplexer_1_out), .sel(not_1_out));
  not not_1 (not_1_out, comparator_1_lt);
  Counter #(.width(32), .max('hffffffff)) counter_1 (
    .Q(counter_1_q), .clk(and_1_out));  // open: load, D, count, carry, clr
  // Probe on counter_1_q
endmodule
